# Fritzing sketch circuit (saved by Fritzing 0.8.3b)
circuit board: 12.192cm x 3.78177cm
breadboards: 2

parts:
  Teensy1 = Teensy 2.0
  U1 = Packages: [package=dil28-3]
  R1 = Resistor [tolerance=±5% resistance=10k package=THT]
  R2 = Resistor [tolerance=±5% resistance=2.2k package=THT]
  R3 = Rotary Potentiometer (Small)
  R4 = Rotary Potentiometer (Small)
  R5 = Rotary Potentiometer (Small)
  S1 = Pushbutton [package="[SMD]"]
  R6 = Resistor [tolerance=±5% resistance=10k package=THT]
  JP1 = Header 5 [package=1x05-1mm-ra]

nets (from the breadboard view):
  GND: Teensy1.GND, U1.GND, U1.SIN, R2.Pin_1, R3.leg2, R4.leg2, R5.leg2, R6.Pin_0, JP1.2
  N1: Teensy1.B1, U1.XLAT
  N2: Teensy1.B2, U1.SCLK
  N3: Teensy1.B3, S1.Pin_1, S1.Pin_2, R6.Pin_1
  N4: Teensy1.C6, U1.GSCLK
  VCC: Teensy1.VCC, U1.DCPRG, U1.VCC, R1.Pin_1, R3.leg1, R4.leg1, R5.leg1, S1.Pin_3, S1.Pin_4
  N5: Teensy1.B5, U1.BLANK, R1.Pin_0
  N6: Teensy1.F4, R4.wiper
  N7: Teensy1.F1, R5.wiper
  N8: Teensy1.F0, R3.wiper
  N9: U1.IREF, R2.Pin_0
