# Fritzing sketch perfboard (saved by Fritzing 0.8.3b)
circuit board: 16.9333cm x 5.64444cm
perfboards: 1

parts:
  Teensy1 = Teensy 2.0
  Power_hub = mystery part, 5 pins [chip_label="Power hub"]
  U1 = Packages: [package=dil28-3]
  U2 = Voltage Regulator - 5V [package="DPak [SMD]"]
  R3 = Resistor [tolerance=±5% resistance=2.2k package=THT]
  R4 = Resistor [tolerance=±5% resistance=10k package=THT]
  Dioder_strip = mystery part, 4 pins [chip_label=Strip]
  Dioder_strip1 = mystery part, 4 pins [chip_label=Strip]  # not connected
  Dioder_strip2 = mystery part, 4 pins [chip_label=Strip]  # not connected
  Dioder_strip3 = mystery part, 4 pins [chip_label=Strip]  # not connected

nets:
  GND: Teensy1.GND, Power_hub.pin1, U2.GND
  N1: Teensy1.B1, U1.SCLK
  N2: Teensy1.B2, U1.SIN
  N3: Teensy1.D3, U1.GSCLK
  N4: Teensy1.B5, U1.XLAT
  N5: Teensy1.B6, U1.BLANK, R4.Pin_0
  N6: Teensy1.VCC, U2.output_voltage
  N7: Power_hub.pin5, U2.input_voltage
  N8: U1.OUT1, Dioder_strip.pin2
  N9: U1.OUT2, Dioder_strip.pin3
  N10: U1.OUT3, Dioder_strip.pin4
  N11: U1.IREF, R3.Pin_0

notes:
  Power
